// Logisim project 7_seg_but_dumb.circ as structural Verilog: 1 circuit, main circuit main
module main (
  input  in_1,
  input  in_2,
  input  in_3,
  input  in_4
);

  wire and_1_out, not_1_out, or_1_out, or_2_out;

  or or_1 (or_1_out, in_1, in_2);
  not not_1 (not_1_out, in_1);
  and and_1 (and_1_out, not_1_out, in_2);
  _7_Segment_Display u_7_segment_display_1 (
    .g(in_2), .f(in_3), .a(in_2), .b(or_1_out), .e(and_1_out), .d(in_2), .c(or_2_out));  // open: dp
  or or_2 (or_2_out, in_3, in_1);
endmodule
