// Logisim project Adders_And_Whatnot.circ as structural Verilog: 4 circuits, main circuit main
module main (
  input  in_1,
  input  in_2,
  input  in_3,
  input  in_4,
  input  in_5,
  input  [7:0] in_6,
  input  [7:0] in_7,
  input  [7:0] A,
  input  [7:0] B,
  output [7:0] out_10,
  output out_11,
  output [7:0] out_12
);

  wire full_adder_1_carry_out, full_adder_1_sum, full_adder_2_carry_out, full_adder_3_carry_out,
       full_adder_4_carry_out, full_adder_5_carry_out, full_adder_6_carry_out, full_adder_7_carry_out,
       full_adder_8_carry_out, half_adder_1_carry_out, half_adder_1_sum, half_adder_2_carry_out;

  LED led_1 (.in(half_adder_1_sum));
  Half_Adder half_adder_1 (.B(in_1), .A(in_2), .Sum(half_adder_1_sum), .Carry_Out(half_adder_1_carry_out));
  LED led_2 (.in(half_adder_1_carry_out));
  LED led_3 (.in(full_adder_1_sum));
  Full_Adder full_adder_1 (
    .Carry_In(in_3), .B(in_4), .A(in_5), .Sum(full_adder_1_sum), .Carry_Out(full_adder_1_carry_out));
  LED led_4 (.in(full_adder_1_carry_out));
  Full_Adder full_adder_2 (
    .Carry_In(full_adder_3_carry_out), .B(B[7]), .A(A[7]), .Sum(out_12[7]), .Carry_Out(full_adder_2_carry_out));
  Full_Adder full_adder_3 (
    .Carry_In(full_adder_4_carry_out), .B(B[6]), .A(A[6]), .Sum(out_12[6]), .Carry_Out(full_adder_3_carry_out));
  Full_Adder full_adder_4 (
    .Carry_In(full_adder_5_carry_out), .B(B[5]), .A(A[5]), .Sum(out_12[5]), .Carry_Out(full_adder_4_carry_out));
  LED OVERFLOW (.in(full_adder_2_carry_out));
  Eight_Bit_Adder eight_bit_adder_1 (.A(in_6), .B(in_7), .Sum(out_10), .Overflow(out_11));
  Full_Adder full_adder_5 (
    .Carry_In(full_adder_6_carry_out), .B(B[4]), .A(A[4]), .Sum(out_12[4]), .Carry_Out(full_adder_5_carry_out));
  Full_Adder full_adder_6 (
    .Carry_In(full_adder_7_carry_out), .B(B[3]), .A(A[3]), .Sum(out_12[3]), .Carry_Out(full_adder_6_carry_out));
  Full_Adder full_adder_7 (
    .Carry_In(full_adder_8_carry_out), .B(B[2]), .A(A[2]), .Sum(out_12[2]), .Carry_Out(full_adder_7_carry_out));
  Full_Adder full_adder_8 (
    .Carry_In(half_adder_2_carry_out), .B(B[1]), .A(A[1]), .Sum(out_12[1]), .Carry_Out(full_adder_8_carry_out));
  Half_Adder half_adder_2 (.B(B[0]), .A(A[0]), .Sum(out_12[0]), .Carry_Out(half_adder_2_carry_out));
endmodule

module Half_Adder (
  input  B,
  input  A,
  output Sum,
  output Carry_Out
);

  xor xor_1 (Sum, B, A);
  and and_1 (Carry_Out, B, A);
endmodule

module Full_Adder (
  input  Carry_In,
  input  B,
  input  A,
  output Sum,
  output Carry_Out
);

  wire and_1_out, and_2_out, xor_2_out;

  and and_1 (and_1_out, B, A);
  xor xor_1 (Sum, Carry_In, xor_2_out);
  and and_2 (and_2_out, Carry_In, xor_2_out);
  xor xor_2 (xor_2_out, B, A);
  xor xor_3 (Carry_Out, and_2_out, and_1_out);
endmodule

module Eight_Bit_Adder (
  input  [7:0] A,
  input  [7:0] B,
  output [7:0] Sum,
  output Overflow
);

  wire full_adder_2_carry_out, full_adder_3_carry_out, full_adder_4_carry_out, full_adder_5_carry_out,
       full_adder_6_carry_out, full_adder_7_carry_out, half_adder_1_carry_out;

  Full_Adder full_adder_1 (.Carry_In(full_adder_2_carry_out), .B(B[7]), .A(A[7]), .Sum(Sum[7]), .Carry_Out(Overflow));
  Full_Adder full_adder_2 (
    .Carry_In(full_adder_3_carry_out), .B(B[6]), .A(A[6]), .Sum(Sum[6]), .Carry_Out(full_adder_2_carry_out));
  Full_Adder full_adder_3 (
    .Carry_In(full_adder_4_carry_out), .B(B[5]), .A(A[5]), .Sum(Sum[5]), .Carry_Out(full_adder_3_carry_out));
  Full_Adder full_adder_4 (
    .Carry_In(full_adder_5_carry_out), .B(B[4]), .A(A[4]), .Sum(Sum[4]), .Carry_Out(full_adder_4_carry_out));
  Full_Adder full_adder_5 (
    .Carry_In(full_adder_6_carry_out), .B(B[3]), .A(A[3]), .Sum(Sum[3]), .Carry_Out(full_adder_5_carry_out));
  Full_Adder full_adder_6 (
    .Carry_In(full_adder_7_carry_out), .B(B[2]), .A(A[2]), .Sum(Sum[2]), .Carry_Out(full_adder_6_carry_out));
  Full_Adder full_adder_7 (
    .Carry_In(half_adder_1_carry_out), .B(B[1]), .A(A[1]), .Sum(Sum[1]), .Carry_Out(full_adder_7_carry_out));
  Half_Adder half_adder_1 (.B(B[0]), .A(A[0]), .Sum(Sum[0]), .Carry_Out(half_adder_1_carry_out));
endmodule
